// Logisim project DesenhoCircuito.circ as structural Verilog: 9 circuits, main circuit halfadder
module halfadder (
  input  A,
  input  B,
  output S,
  output Co
);

  xor xor_1 (S, A, B);
  and and_1 (Co, B, B, A);
endmodule

module fulladder (
  input  Ci,
  input  a,
  input  b,
  output S,
  output Co
);

  wire halfadder_1_co, halfadder_1_s, halfadder_2_co;

  halfadder halfadder_1 (.A(a), .B(b), .S(halfadder_1_s), .Co(halfadder_1_co));
  halfadder halfadder_2 (.A(Ci), .B(halfadder_1_s), .S(S), .Co(halfadder_2_co));
  or or_1 (Co, halfadder_2_co, halfadder_1_co);
endmodule

module adder4bit (
  input  Ci,
  input  A0,
  input  B0,
  input  A1,
  input  B1,
  input  A2,
  input  B2,
  input  A3,
  input  B3,
  output S0,
  output S1,
  output S2,
  output S3,
  output C4
);

  wire fulladder_1_co, fulladder_2_co, fulladder_3_co;

  fulladder fulladder_1 (.Ci(Ci), .a(B0), .b(A0), .S(S0), .Co(fulladder_1_co));
  fulladder fulladder_2 (.Ci(fulladder_1_co), .a(B1), .b(A1), .S(S1), .Co(fulladder_2_co));
  fulladder fulladder_3 (.Ci(fulladder_2_co), .a(B2), .b(A2), .S(S2), .Co(fulladder_3_co));
  fulladder fulladder_4 (.Ci(fulladder_3_co), .a(B3), .b(A3), .S(S3), .Co(C4));
endmodule

module adder_8bit (
  input  C0,
  input  A0,
  input  B0,
  input  A1,
  input  B1,
  input  A2,
  input  B2,
  input  A3,
  input  B3,
  input  A4,
  input  B4,
  input  A5,
  input  B5,
  input  A6,
  input  B6,
  input  A7,
  input  B7,
  output S0,
  output S1,
  output S2,
  output S3,
  output S4,
  output S5,
  output S6,
  output S7,
  output C8
);

  wire adder4bit_1_c4;

  adder4bit adder4bit_1 (
    .Ci(C0), .A0(A0), .B0(B0), .A1(A1), .B1(B1), .A2(A2), .B2(B2), .A3(A3), .B3(B3), .S0(S0), .S1(S1),
    .S2(S2), .S3(S3), .C4(adder4bit_1_c4));
  adder4bit adder4bit_2 (
    .Ci(adder4bit_1_c4), .A0(A4), .B0(B4), .A1(A5), .B1(B5), .A2(A6), .B2(B6), .A3(A7), .B3(B7), .S0(S4),
    .S1(S5), .S2(S6), .S3(S7), .C4(C8));
endmodule

module Somador_subtrador (
  input  m,
  input  A0,
  input  B0,
  input  A1,
  input  B1,
  input  A2,
  input  B2,
  input  A3,
  input  B3,
  input  A4,
  input  B4,
  input  A5,
  input  B5,
  input  A6,
  input  B6,
  input  A7,
  input  B7,
  input  A8,
  input  B8,
  input  A9,
  input  B9,
  input  A10,
  input  B10,
  input  A11,
  input  B11,
  input  A12,
  input  B12,
  input  A13,
  input  B13,
  input  A14,
  input  B14,
  input  A15,
  input  B15,
  output S0,
  output S1,
  output S2,
  output S3,
  output S4,
  output S5,
  output S6,
  output S7,
  output S8,
  output S9,
  output S10,
  output S11,
  output S12,
  output S13,
  output S14,
  output S15,
  output C16
);

  wire adder_8bit_2_c8, nor_1_out, nor_2_out, xor_1_out, xor_2_out, xor_3_out, xor_4_out, xor_5_out,
       xor_6_out, xor_7_out, xor_8_out, xor_9_out, xor_10_out, xor_11_out, xor_12_out, xor_13_out, xor_14_out;

  xor xor_1 (xor_1_out, m, B0);
  xor xor_2 (xor_2_out, m, B1);
  xor xor_3 (xor_3_out, m, B2);
  xor xor_4 (xor_4_out, B3, m);
  xor xor_5 (xor_5_out, B4, m);
  xor xor_6 (xor_6_out, B5, m);
  xor xor_7 (xor_7_out, B6, m);
  xor xor_8 (xor_8_out, B7, m);
  nor nor_1 (nor_1_out, B8, m);
  nor nor_2 (nor_2_out, B9, m);
  xor xor_9 (xor_9_out, B10, m);
  xor xor_10 (xor_10_out, m, B11);
  xor xor_11 (xor_11_out, m, B12);
  xor xor_12 (xor_12_out, m, B14);
  xor xor_13 (xor_13_out, B15, m);
  xor xor_14 (xor_14_out, m, B13);
  adder_8bit adder_8bit_1 (
    .C0(adder_8bit_2_c8), .A0(A8), .B0(nor_1_out), .A1(A9), .B1(nor_2_out), .A2(A10), .B2(xor_9_out),
    .A3(A11), .B3(xor_10_out), .A4(A12), .B4(xor_11_out), .A5(A13), .B5(xor_14_out), .A6(A14),
    .B6(xor_12_out), .A7(A15), .B7(xor_13_out), .S0(S8), .S1(S9), .S2(S10), .S3(S11), .S4(S12), .S5(S13),
    .S6(S14), .S7(S15), .C8(C16));
  adder_8bit adder_8bit_2 (
    .C0(m), .A0(A0), .B0(xor_1_out), .A1(A1), .B1(xor_2_out), .A2(A2), .B2(xor_3_out), .A3(A3),
    .B3(xor_4_out), .A4(A4), .B4(xor_5_out), .A5(A5), .B5(xor_6_out), .A6(A6), .B6(xor_7_out), .A7(A7),
    .B7(xor_8_out), .S0(S0), .S1(S1), .S2(S2), .S3(S3), .S4(S4), .S5(S5), .S6(S6), .S7(S7),
    .C8(adder_8bit_2_c8));
endmodule

module Demux (
  input  B,
  input  OP,
  input  nB,
  output S
);

  wire and_1_out, and_2_out, not_1_out;

  not not_1 (not_1_out, OP);
  and and_1 (and_1_out, B, not_1_out);
  and and_2 (and_2_out, OP, nB);
  or or_1 (S, and_1_out, and_2_out);
endmodule

module \negação_b  (
  input  B0,
  input  B1,
  input  B2,
  input  B3,
  input  B4,
  input  B5,
  input  B6,
  input  B7,
  output S0,
  output S1,
  output S2,
  output S3,
  output S4,
  output S5,
  output S6,
  output S7
);

  not not_1 (S0, B0);
  not not_2 (S1, B1);
  not not_3 (S2, B2);
  not not_4 (S3, B3);
  not not_5 (S4, B4);
  not not_6 (S5, B5);
  not not_7 (S6, B6);
  not not_8 (S7, B7);
endmodule

module demux2x8 (
  input  OP,
  input  B0,
  input  B1,
  input  B2,
  input  B3,
  input  B4,
  input  B5,
  input  B6,
  input  B7,
  output B0_2,
  output B1_2,
  output B2_2,
  output B3_2,
  output B4_2,
  output B5_2,
  output B6_2,
  output B7_2
);

  wire not_1_out, not_2_out, not_3_out, not_4_out, not_5_out, not_6_out, not_7_out, not_8_out;

  not not_1 (not_1_out, B0);
  not not_2 (not_2_out, B1);
  not not_3 (not_3_out, B2);
  not not_4 (not_4_out, B3);
  not not_5 (not_5_out, B4);
  not not_6 (not_6_out, B5);
  not not_7 (not_7_out, B6);
  not not_8 (not_8_out, B7);
  Demux demux_1 (.B(B0), .OP(OP), .nB(not_1_out), .S(B0_2));
  Demux demux_2 (.B(B1), .OP(OP), .nB(not_2_out), .S(B1_2));
  Demux demux_3 (.B(B2), .OP(OP), .nB(not_3_out), .S(B2_2));
  Demux demux_4 (.B(B3), .OP(OP), .nB(not_4_out), .S(B3_2));
  Demux demux_5 (.B(B4), .OP(OP), .nB(not_5_out), .S(B4_2));
  Demux demux_6 (.B(B5), .OP(OP), .nB(not_6_out), .S(B5_2));
  Demux demux_7 (.B(B6), .OP(OP), .nB(not_7_out), .S(B6_2));
  Demux demux_8 (.B(B7), .OP(OP), .nB(not_8_out), .S(B7_2));
endmodule

module overflow (
  input  A,
  input  B,
  input  S,
  output Overflow
);

  wire and_1_out, and_2_out, not_1_out, not_2_out, not_3_out;

  not not_1 (not_1_out, B);
  not not_2 (not_2_out, A);
  not not_3 (not_3_out, S);
  and and_1 (and_1_out, S, not_1_out, not_2_out);
  and and_2 (and_2_out, not_3_out, B, A);
  or or_1 (Overflow, and_1_out, and_2_out);
endmodule
